# Fritzing sketch smart Cm (saved by Fritzing 0.9.3b)
breadboards: 1

parts:
  Componente1 = Arduino Uno (Rev3)
  LED1 = LED - 5mm [color="Red (633nm)" package="5 mm [THT]"]
  LED2 = LED - 5mm [color="Red (633nm)" package="5 mm [THT]"]
  LED3 = LED - 5mm [color="Red (633nm)" package="5 mm [THT]"]
  R1 = Resistor [tolerance=±5% resistance=220 package=THT]
  R2 = Resistor [tolerance=±5% resistance=220 package=THT]
  R3 = Resistor [tolerance=±5% resistance=220 package=THT]
  S1 = Pushbutton [package="[THT]"]
  HC-SR04_Sensor_1 = HC-SR04 Ultrasonic Distance Sensor
  R4 = Resistor [tolerance=±5% resistance=10k package=THT]
  R5 = Rotary Potentiometer (Small) [maximum_resistance=100kΩ package=THT]
  Sensore_PIR_HC-SR502 = HC-SR501 Body Sensor Module

nets:
  N1: Componente1.A0, R5.wiper
  N2: Componente1.D8, R3.Pin_1
  N3: Componente1.D9_PWM, R2.Pin_1
  N4: Componente1.D10_PWM/SS, R1.Pin_1
  GND: Componente1.GND, LED1.anode, LED2.anode, LED3.anode, HC-SR04_Sensor_1.GND, R4.Pin_1, R5.leg1, Sensore_PIR_HC-SR502.GND
  N5: Componente1.D1/TX, Sensore_PIR_HC-SR502.OUT
  N6: Componente1.D3_PWM, HC-SR04_Sensor_1.TRIG
  N7: Componente1.D4, HC-SR04_Sensor_1.ECHO
  N8: Componente1.D7, S1.Pin_3, S1.Pin_4, R4.Pin_0
  VCC: Componente1.5V, S1.Pin_2, HC-SR04_Sensor_1.VCC, R5.leg2, Sensore_PIR_HC-SR502.VCC
  N9: LED1.cathode, R1.Pin_0
  N10: LED2.cathode, R2.Pin_0
  N11: LED3.cathode, R3.Pin_0

custom parts:
  HC-SR501 Body Sensor Module: Pyroelectric Infrared PIR Motion Sensor Detector Module
